# Fritzing sketch zapojeni (saved by Fritzing 0.9.2b)
breadboards: 1

parts:
  Part1 = Arduino Uno (Rev3) - ICSP
  Matrix_keypad1 = KEYPAD 4x4  # not connected
  R1 = Resistor [tolerance=±5% resistance=220 package=THT]
  R2 = Resistor [tolerance=±5% resistance=220 package=THT]
  C1 = Electrolytic Capacitor [capacitance=1µF package="100 mil [THT, electrolytic]"]
  SPKR1 = Loudspeaker

nets:
  N1: Part1.D6_PWM, R1.Pin_0, C1.+
  N2: Part1.GND, C1.-, SPKR1.pin1
  N3: R1.Pin_1, R2.Pin_1
  N4: R2.Pin_0, SPKR1.pin2

custom parts:
  KEYPAD 4x4: Matrix keypad 16 buttons, 4 rows x 4 columns
